# Fritzing sketch NumberMagic (saved by Fritzing 0.9.3b)
breadboards: 1

parts:
  Composant1 = Arduino Uno (Rev3)
  LCD1 = LCD screen
  Keypad4x1 = Keypad Membran 4x4
  U1 = POT [package=alps_pot]
  U2 = MAX7219 [package=dil24]
  LED1 = 5641AS-1 [part_number=5641AS-1 package="DIP (Dual Inline) [THT]"]
  R1 = Resistor [tolerance=±5% resistance=4.7k package=THT]
  R2 = Resistor [tolerance=±5% resistance=22k package=THT]
  C1 = Electrolytic Capacitor [capacitance=10µF voltage=50V package="100 mil [THT, electrolytic]"]
  C2 = Ceramic Capacitor [capacitance=100nF package="100 mil [THT, multilayer]"]
  C3 = Ceramic Capacitor [capacitance=100nF package="100 mil [THT, multilayer]"]

nets:
  N1: Composant1.A0, LCD1.DB4, U2.DIN
  N2: Composant1.A1, LCD1.DB5
  N3: Composant1.A2, LCD1.DB6
  N4: Composant1.A3, LCD1.DB7
  N5: Composant1.A4/SDA, LCD1.RS
  N6: Composant1.A5/SCL, LCD1.E
  N7: Composant1.D8, Keypad4x1.Pin2
  N8: Composant1.D9_PWM, Keypad4x1.Pin1
  N9: Composant1.D12/MISO, U2.CLK
  N10: Composant1.D13/SCK, U2.LOAD
  N11: Composant1.D2, Keypad4x1.Pin8
  N12: Composant1.D3_PWM, Keypad4x1.Pin7
  N13: Composant1.D4, Keypad4x1.Pin6
  N14: Composant1.D5_PWM, Keypad4x1.Pin5
  N15: Composant1.D6_PWM, Keypad4x1.Pin4
  N16: Composant1.D7, Keypad4x1.Pin3
  N17: Composant1.3V3, LCD1.LED+
  5V: Composant1.5V, LCD1.VDD, U1.A, U2.VCC, R2.Pin_0, C1.+, C2.1, C3.1
  GND: Composant1.GND, LCD1.VSS, LCD1.R/W, LCD1.LED-, U1.E, U2.GND, U2.GND2, C1.-, C2.0, C3.0
  N18: LCD1.V0, U1.S
  N19: U2.DIG0, LED1.cat1
  N20: U2.DIG2, LED1.cat3
  N21: U2.DIG3, LED1.cat4
  N22: U2.DIG1, LED1.cat2
  N23: U2.SEGA, LED1.anA
  N24: U2.SEGF, LED1.anF
  N25: U2.SEGB, LED1.anB
  N26: U2.SEGG, LED1.anG
  N27: U2.ISET, R1.Pin_1
  N28: U2.SEGC, LED1.anC
  N29: U2.SEGE, LED1.anE
  N30: U2.SEGDP, LED1.anDP
  N31: U2.SEGD, LED1.anD
  N32: R1.Pin_0, R2.Pin_1

custom parts:
  Keypad Membran 4x4: Membrane Keypad 4x4 Matrix
  5641AS-1: 4 digit 7 segment common cathode LED display
